# Fritzing sketch KlingelV4 (saved by Fritzing 0.9.5d)
circuit board: 8.46667cm x 5.64444cm
perfboards: 1

parts:
  U2 = 2RelayModule
  U1 = LuaNode32 / ESP32 [part_number=ESP32S-PIN30]
  J4 = Camdenboss CTB0158-5 [part_number=CTB0158-5 package=THT]
  J5 = Camdenboss CTB0158-2 [part_number=CTB0158-2 package=THT]
  R1 = Resistor [tolerance=±5% resistance=1000 package="2010 [SMD]"]
  OC2 = Sharp PC817 [package=THT]
  OC1 = Sharp PC817 [package=THT]
  J6 = Camdenboss CTB0158-3 [part_number=CTB0158-3 package=THT]
  J7 = Camdenboss CTB0158-2 [part_number=CTB0158-2 package=THT]
  J8 = Camdenboss CTB0158-3 [part_number=CTB0158-3 package=THT]
  J9 = Camdenboss CTB0158-2 [part_number=CTB0158-2 package=THT]
  U3 = M16 [package=1x16_machine-pin-header_lock.004]
  U4 = M16 [package=1x16_machine-pin-header_lock.004]
  R2 = Resistor [tolerance=±5% resistance=5100 package="2010 [SMD]"]

nets:
  N1: U2.IN2, U1.D25, J8.pin2, J8.terminal_2, U4.8
  WF26-P3: U2.NO1, J4.pin3
  WF26-P2: U2.MAIN1, J4.pin2
  N2: U2.IN1, U1.D26, J8.pin1, J8.terminal_1, U4.9
  GND: U2.GND#6, U1.GND, R1.Pin_0, J9.pin2, J9.terminal_2, U3.14, U4.14
  WF26-IN-P4: U2.NC2, J5.pin1, OC1.Pin_1, J6.terminal_2, J7.pin1, J7.terminal_1
  WF26-P4: U2.MAIN2, J4.pin4
  N3: U2.JD-VCC, U1.Vin, J9.pin1, J9.terminal_1, U4.15
  3.3V: U2.VCC, U1.3V3, J8.terminal_3, U3.15
  N4: U1.EN, U4.1
  N5: U1.VP, U4.2
  N6: U1.VN, U4.3
  N7: U1.D34, U4.4
  N8: U1.D35, U4.5
  N9: U1.D32, OC2.Pin_4, U4.6
  N10: U1.D33, OC1.Pin_4, U4.7
  N11: U1.D27, U4.10
  N12: U1.D14, U4.11
  N13: U1.D12, U4.12
  N14: U1.D13, U4.13
  N15: U1.D15, U3.13
  N16: U1.D2, U3.12
  N17: U1.D4, U3.11
  N18: U1.RX2, U3.10
  N19: U1.TX2, U3.9
  N20: U1.D5, U3.8
  N21: U1.D18, U3.7
  N22: U1.D19, U3.6
  N23: U1.D21, U3.5
  N24: U1.RX0, U3.4
  N25: U1.TX0, U3.3
  N26: U1.D22, U3.2
  N27: U1.D23, U3.1
  WF26-P1: J4.pin1, J7.pin2, J7.terminal_2, R2.Pin_0
  WF26-P5: J4.pin5, J5.pin2, OC2.Pin_1, J6.pin1, J6.pin3, J6.terminal_1, J6.terminal_3
  N28: R1.Pin_1, OC2.Pin_3, OC1.Pin_3
  N29: OC2.Pin_2, OC1.Pin_2, R2.Pin_1

custom parts:
  2RelayModule: 2 relay arduino module SONGLE SRD05VDC-SL-C
  LuaNode32 / ESP32: New Image for LuaNode32 DOIT ESP32 DEVKIT V1. Base parts from LuaNode32 / ESP32 ESP32 based LuaNode32 by G.Noorlander DOIT Esp32 DevKit v1 (30 pins long, 11 pins width) by Werner Rothschopf (modified by vanepp Dec 2018)
